// Logisim project ula.circ as structural Verilog: 4 circuits, main circuit main
module main (
  input  [31:0] A,
  input  [4:0] in_2,
  input  [31:0] B,
  output [31:0] S,
  output OverFlow
);

  wire and_1_out, not_1_out;
  wire [1:0] multiplexer_1_out, ula_cel_1_cout, ula_cel_6_cout, ula_cel_7_cout, ula_cel_8_cout,
       ula_cel_10_cout, ula_cel_11_cout, ula_cel_12_cout;
  wire [1:1] ula_cel_13_cout, ula_cel_14_cout, ula_cel_15_cout, ula_cel_16_cout, ula_cel_17_cout,
       ula_cel_18_cout, ula_cel_19_cout, ula_cel_20_cout, ula_cel_21_cout, ula_cel_22_cout, ula_cel_23_cout,
       ula_cel_24_cout, ula_cel_25_cout, ula_cel_26_cout, ula_cel_27_cout, ula_cel_28_cout, ula_cel_32_cout;

  and and_1 (and_1_out, ~in_2[4], ~in_2[3], in_2[2], in_2[1], ~in_2[0]);  // AND_Gate
  not not_1 (not_1_out, 1'b0);
  Multiplexer #(.enable("false")) multiplexer_1 (
    .in0(1'b0), .in1(not_1_out), .out(multiplexer_1_out[0]), .sel(and_1_out));
  ula_cel ula_cel_1 (.Cin(multiplexer_1_out), .a(A[0]), .b(B[0]), .Select(in_2), .S(S[0]), .Cout(ula_cel_1_cout[0]));
  ula_cel ula_cel_2 (.Cin(ula_cel_6_cout), .a(A[8]), .b(B[8]), .Select(in_2), .S(S[8]), .Cout(ula_cel_10_cout[0]));
  ula_cel ula_cel_3 (.Cin(ula_cel_7_cout), .a(A[16]), .b(B[16]), .Select(in_2), .S(S[16]), .Cout(ula_cel_11_cout[0]));
  ula_cel ula_cel_4 (.Cin(ula_cel_8_cout), .a(A[24]), .b(B[24]), .Select(in_2), .S(S[24]), .Cout(ula_cel_12_cout[0]));
  ula_cel ula_cel_5 (.Cin(ula_cel_1_cout), .a(A[1]), .b(B[1]), .Select(in_2), .S(S[1]), .Cout(multiplexer_1_out[1]));
  ula_cel ula_cel_6 (.Cin(ula_cel_10_cout), .a(A[9]), .b(B[9]), .Select(in_2), .S(S[9]), .Cout(ula_cel_6_cout[1]));
  ula_cel ula_cel_7 (.Cin(ula_cel_11_cout), .a(A[17]), .b(B[17]), .Select(in_2), .S(S[17]), .Cout(ula_cel_7_cout[1]));
  ula_cel ula_cel_8 (.Cin(ula_cel_12_cout), .a(A[25]), .b(B[25]), .Select(in_2), .S(S[25]), .Cout(ula_cel_8_cout[1]));
  ula_cel ula_cel_9 (
    .Cin({ula_cel_13_cout[1], multiplexer_1_out[1]}), .a(A[2]), .b(B[2]), .Select(in_2), .S(S[2]),
    .Cout(ula_cel_1_cout[1]));
  ula_cel ula_cel_10 (
    .Cin({ula_cel_14_cout[1], ula_cel_6_cout[1]}), .a(A[10]), .b(B[10]), .Select(in_2), .S(S[10]),
    .Cout(ula_cel_10_cout[1]));
  ula_cel ula_cel_11 (
    .Cin({ula_cel_15_cout[1], ula_cel_7_cout[1]}), .a(A[18]), .b(B[18]), .Select(in_2), .S(S[18]),
    .Cout(ula_cel_11_cout[1]));
  ula_cel ula_cel_12 (
    .Cin({ula_cel_16_cout[1], ula_cel_8_cout[1]}), .a(A[26]), .b(B[26]), .Select(in_2), .S(S[26]),
    .Cout(ula_cel_12_cout[1]));
  ula_cel ula_cel_13 (
    .Cin({ula_cel_17_cout[1], ula_cel_1_cout[1]}), .a(A[3]), .b(B[3]), .Select(in_2), .S(S[3]),
    .Cout(ula_cel_13_cout[1]));
  ula_cel ula_cel_14 (
    .Cin({ula_cel_18_cout[1], ula_cel_10_cout[1]}), .a(A[11]), .b(B[11]), .Select(in_2), .S(S[11]),
    .Cout(ula_cel_14_cout[1]));
  ula_cel ula_cel_15 (
    .Cin({ula_cel_19_cout[1], ula_cel_11_cout[1]}), .a(A[19]), .b(B[19]), .Select(in_2), .S(S[19]),
    .Cout(ula_cel_15_cout[1]));
  ula_cel ula_cel_16 (
    .Cin({ula_cel_20_cout[1], ula_cel_12_cout[1]}), .a(A[27]), .b(B[27]), .Select(in_2), .S(S[27]),
    .Cout(ula_cel_16_cout[1]));
  ula_cel ula_cel_17 (
    .Cin({ula_cel_21_cout[1], ula_cel_13_cout[1]}), .a(A[4]), .b(B[4]), .Select(in_2), .S(S[4]),
    .Cout(ula_cel_17_cout[1]));
  ula_cel ula_cel_18 (
    .Cin({ula_cel_22_cout[1], ula_cel_14_cout[1]}), .a(A[12]), .b(B[12]), .Select(in_2), .S(S[12]),
    .Cout(ula_cel_18_cout[1]));
  ula_cel ula_cel_19 (
    .Cin({ula_cel_23_cout[1], ula_cel_15_cout[1]}), .a(A[20]), .b(B[20]), .Select(in_2), .S(S[20]),
    .Cout(ula_cel_19_cout[1]));
  ula_cel ula_cel_20 (
    .Cin({ula_cel_24_cout[1], ula_cel_16_cout[1]}), .a(A[28]), .b(B[28]), .Select(in_2), .S(S[28]),
    .Cout(ula_cel_20_cout[1]));
  ula_cel ula_cel_21 (
    .Cin({ula_cel_25_cout[1], ula_cel_17_cout[1]}), .a(A[5]), .b(B[5]), .Select(in_2), .S(S[5]),
    .Cout(ula_cel_21_cout[1]));
  ula_cel ula_cel_22 (
    .Cin({ula_cel_26_cout[1], ula_cel_18_cout[1]}), .a(A[13]), .b(B[13]), .Select(in_2), .S(S[13]),
    .Cout(ula_cel_22_cout[1]));
  ula_cel ula_cel_23 (
    .Cin({ula_cel_27_cout[1], ula_cel_19_cout[1]}), .a(A[21]), .b(B[21]), .Select(in_2), .S(S[21]),
    .Cout(ula_cel_23_cout[1]));
  ula_cel ula_cel_24 (
    .Cin({ula_cel_28_cout[1], ula_cel_20_cout[1]}), .a(A[29]), .b(B[29]), .Select(in_2), .S(S[29]),
    .Cout(ula_cel_24_cout[1]));
  ula_cel ula_cel_25 (
    .Cin({ula_cel_6_cout[0], ula_cel_21_cout[1]}), .a(A[6]), .b(B[6]), .Select(in_2), .S(S[6]),
    .Cout(ula_cel_25_cout[1]));
  ula_cel ula_cel_26 (
    .Cin({ula_cel_7_cout[0], ula_cel_22_cout[1]}), .a(A[14]), .b(B[14]), .Select(in_2), .S(S[14]),
    .Cout(ula_cel_26_cout[1]));
  ula_cel ula_cel_27 (
    .Cin({ula_cel_8_cout[0], ula_cel_23_cout[1]}), .a(A[22]), .b(B[22]), .Select(in_2), .S(S[22]),
    .Cout(ula_cel_27_cout[1]));
  ula_cel ula_cel_28 (
    .Cin({ula_cel_32_cout[1], ula_cel_24_cout[1]}), .a(A[30]), .b(B[30]), .Select(in_2), .S(S[30]),
    .Cout(ula_cel_28_cout[1]));
  ula_cel ula_cel_29 (
    .Cin({ula_cel_10_cout[0], ula_cel_25_cout[1]}), .a(A[7]), .b(B[7]), .Select(in_2), .S(S[7]),
    .Cout(ula_cel_6_cout[0]));
  ula_cel ula_cel_30 (
    .Cin({ula_cel_11_cout[0], ula_cel_26_cout[1]}), .a(A[15]), .b(B[15]), .Select(in_2), .S(S[15]),
    .Cout(ula_cel_7_cout[0]));
  ula_cel ula_cel_31 (
    .Cin({ula_cel_12_cout[0], ula_cel_27_cout[1]}), .a(A[23]), .b(B[23]), .Select(in_2), .S(S[23]),
    .Cout(ula_cel_8_cout[0]));
  ula_cel ula_cel_32 (
    .Cin({1'b0, ula_cel_28_cout[1]}), .a(A[31]), .b(B[31]), .Select(in_2), .S(S[31]),
    .Cout(ula_cel_32_cout[1]));
  overflow overflow_1 (.OpeCod(in_2), .Cin(ula_cel_32_cout[1]), .S(S[31]), .b(B[31]), .a(A[31]), .OverFlow(OverFlow));

  // Notes on the sheet:
  //   00000 - And
  //   00001 - Or
  //   00010 - XOR
  //   00011 - NAND
  //   00100 - Soma naturais
  //   00101 - Soma inteiros
  //   00110 - Subtração
  //   00111 - SLL
  //   01000 - SRL
endmodule

module ula_cel (
  input  a,
  input  b,
  input  [1:0] Cin,
  input  [4:0] Select,
  output S,
  output Cout
);

  wire and_1_out, and_2_out, and_3_out, full_adder_1_cout, full_adder_1_s, multiplexer_1_out, nand_1_out,
       or_1_out, or_2_out, xor_1_out;

  Multiplexer #(.enable("false")) multiplexer_1 (.in0(Cin[0]), .in1(Cin[1]), .out(multiplexer_1_out), .sel(and_1_out));
  and and_1 (and_1_out, ~Select[0], ~Select[1], ~Select[2], Select[3], ~Select[4]);  // AND_Gate
  and and_2 (and_2_out, a, b);
  or or_1 (or_1_out, a, b);
  xor xor_1 (xor_1_out, a, b);
  nand nand_1 (nand_1_out, a, b);
  full_adder full_adder_1 (
    .in_3(Select), .Cin(multiplexer_1_out), .a(a), .b(b), .s(full_adder_1_s), .Cout(full_adder_1_cout));
  and and_3 (and_3_out, Select[0], Select[1], Select[2], ~Select[3], ~Select[4]);  // AND_Gate
  or or_2 (or_2_out, and_3_out, and_1_out);
  Multiplexer #(.enable("false")) multiplexer_2 (.in0(full_adder_1_cout), .in1(a), .out(Cout), .sel(or_2_out));
  Multiplexer #(.select(5), .enable("false")) multiplexer_3 (
    .in0(and_2_out), .in1(or_1_out), .in2(xor_1_out), .in3(nand_1_out), .in4(full_adder_1_s),
    .in5(full_adder_1_s), .in6(full_adder_1_s), .in7(multiplexer_1_out), .in8(multiplexer_1_out), .out(S),
    .sel(Select));  // open: in9, in10, in11, in12, in13, in14, in15, in16, in17, in18, in19, in20, in21, in22, in23, in24, in25, in26, in27, in28, in29, in30, in31

  // Notes on the sheet:
  //   00000 - And
  //   00001 - Or
  //   00010 - XOR
  //   00011 - NAND
  //   00100 - Soma naturais
  //   00101 - Soma inteiros
  //   00110 - Subtração
  //   00111 - SLL
  //   01000 - SRL
endmodule

module full_adder (
  input  a,
  input  b,
  input  [4:0] in_3,
  input  Cin,
  output Cout,
  output s
);

  wire and_1_out, and_2_out, and_3_out, and_4_out, and_5_out, multiplexer_1_out, not_1_out, xor_1_out;

  and and_1 (and_1_out, ~in_3[0], in_3[1], in_3[2], ~in_3[3], ~in_3[4]);  // AND_Gate
  not not_1 (not_1_out, b);
  Multiplexer #(.enable("false")) multiplexer_1 (.in0(b), .in1(not_1_out), .out(multiplexer_1_out), .sel(and_1_out));
  xor xor_1 (xor_1_out, a, multiplexer_1_out);
  xor xor_2 (s, xor_1_out, Cin);
  and and_2 (and_2_out, ~a, multiplexer_1_out, Cin);  // AND_Gate
  and and_3 (and_3_out, a, ~multiplexer_1_out, Cin);  // AND_Gate
  and and_4 (and_4_out, a, multiplexer_1_out, ~Cin);  // AND_Gate
  and and_5 (and_5_out, a, multiplexer_1_out, Cin);
  or or_1 (Cout, and_2_out, and_3_out, and_4_out, and_5_out);
endmodule

module overflow (
  input  Cin,
  input  S,
  input  b,
  input  a,
  input  [4:0] OpeCod,
  output OverFlow
);

  wire and_1_out, and_2_out, and_3_out, and_4_out, or_1_out, or_2_out;

  and and_1 (and_1_out, OpeCod[0], ~OpeCod[1], OpeCod[2], ~OpeCod[3], ~OpeCod[4]);  // AND_Gate
  and and_2 (and_2_out, ~OpeCod[0], OpeCod[1], OpeCod[2], ~OpeCod[3], ~OpeCod[4]);  // AND_Gate
  and and_3 (and_3_out, ~S, b, a);  // AND_Gate
  and and_4 (and_4_out, S, ~b, ~a);  // AND_Gate
  or or_1 (or_1_out, and_1_out, and_2_out);
  or or_2 (or_2_out, and_3_out, and_4_out);
  Multiplexer #(.enable("false")) multiplexer_1 (.in0(Cin), .in1(or_2_out), .out(OverFlow), .sel(or_1_out));

  // Notes on the sheet:
  //   00100 - Soma naturais
  //   00101 - Soma inteiros
  //   00110 - Subtração
endmodule
